// Digital circuit Memory_selection_logic.dig as structural Verilog
module Memory_selection_logic (
  output out_1
);

  wire and_1_out, and_2_out, and_3_out, and_4_out, and_5_out, D8, I0, I1, I1_t, R, T1, T3, T4, T5;

  and and_1 (and_1_out, R, T1);
  and and_2 (and_2_out, D8, T5);
  and and_3 (and_3_out, T4, I1_t, I0);
  and and_4 (and_4_out, T4, I0, I1);
  and and_5 (and_5_out, I1, I0, T3);
  or or_1 (out_1, and_1_out, and_2_out, and_3_out, and_4_out, and_5_out);
endmodule
