// Digital circuit alu.dig as structural Verilog
module alu (
  output out_1
);

  wire AC, add_1_c_o, add_1_s, and_1_out, and_2_out, and_3_out, and_4_out, and_5_out, and_6_out, and_7_out,
       Ci, D0, D1, D2, D3, D4, D5, D6, DR, sub_1_c_o, sub_1_s, T5;

  Add add_1 (.a(AC), .b(AC), .c_i(Ci), .s(add_1_s), .c_o(add_1_c_o));
  Sub sub_1 (.a(AC), .b(DR), .c_i(Ci), .s(sub_1_s), .c_o(sub_1_c_o));
  and and_1 (and_1_out, T5, D0, AC, DR);
  and and_2 (and_2_out, T5, add_1_s, D2);
  and and_3 (and_3_out, DR, T5, D4);
  and and_4 (and_4_out, DR, AC, T5, D1);
  and and_5 (and_5_out, sub_1_s, T5, D3);
  and and_6 (and_6_out, AC, D5, T5);
  and and_7 (and_7_out, T5, D6);
  or or_1 (out_1, and_1_out, and_2_out, and_3_out, and_4_out, and_5_out, and_6_out, and_7_out);

  // Notes on the sheet:
  //   ALU
endmodule
