// Digital circuit common_bus.dig as structural Verilog
module common_bus (
  input  clk
);

  wire AC_Load_Line_Out, AR_Load_Line_Out, Bus_Selection_0, Bus_Selection_1, Bus_Selection_2,
       DR_Load_Line_Out, INPR_Load_Line_Out, IR_Load_Line_Out, memory_control_1_read, memory_control_1_write,
       OUTR_Load_Line_Out, PC_Load_Line_Out, TR_Load_Line_Out;
  wire [7:0] ALU_Input_3, To_Output_Device;
  wire [11:0] AR_q, multiplexer_1_out, PC_q;
  wire [15:0] ALU_Input_1, ALU_Input_2, ALU_Output, IR_q, Memory_d, TR_q;
  wire [15:12] multiplexer_1_out_2;

  memory_control memory_control_1 (.Write(memory_control_1_write), .Read(memory_control_1_read));
  RAMDualPort #(.AddrBits(12), .Bits(16)) Memory (
    .A(AR_q), .Din({multiplexer_1_out_2, multiplexer_1_out}), .str(memory_control_1_write), .C(clk),
    .ld(memory_control_1_read), .D(Memory_d));
  Register #(.Bits(12)) AR (.D(multiplexer_1_out), .C(clk), .en(AR_Load_Line_Out), .Q(AR_q));
  Register #(.Bits(12), .isProgramCounter("true")) PC (.D(multiplexer_1_out), .C(clk), .en(PC_Load_Line_Out), .Q(PC_q));
  Register #(.Bits(16)) DR (
    .D({multiplexer_1_out_2, multiplexer_1_out}), .C(clk), .en(DR_Load_Line_Out), .Q(ALU_Input_1));
  Register #(.Bits(16)) AC (.D(ALU_Output), .C(clk), .en(AC_Load_Line_Out), .Q(ALU_Input_2));
  Register #(.Bits(8)) INPR (.D(multiplexer_1_out[7:0]), .C(clk), .en(INPR_Load_Line_Out), .Q(ALU_Input_3));
  Register #(.Bits(16)) IR (.D({multiplexer_1_out_2, multiplexer_1_out}), .C(clk), .en(IR_Load_Line_Out), .Q(IR_q));
  Register #(.Bits(16)) TR (.D({multiplexer_1_out_2, multiplexer_1_out}), .C(clk), .en(TR_Load_Line_Out), .Q(TR_q));
  Register #(.Bits(8)) OUTR (.D(multiplexer_1_out[7:0]), .C(clk), .en(OUTR_Load_Line_Out), .Q(To_Output_Device));
  Multiplexer #(.Selector_Bits(3), .Bits(16)) multiplexer_1 (
    .sel({Bus_Selection_0, Bus_Selection_1, Bus_Selection_2}), .in_0({16{1'b0}}), .in_1({4'b0000, AR_q}),
    .in_2({4'b0000, PC_q}), .in_3(ALU_Input_1), .in_4(ALU_Input_2), .in_5(IR_q), .in_6(TR_q),
    .in_7(Memory_d), .out({multiplexer_1_out_2, multiplexer_1_out}));

  // Other names for the same wires on the sheet: Master_Clock = clk

  // Notes on the sheet:
  //   Common Bus
endmodule
