// Digital circuit common_bus_2.dig as structural Verilog
module common_bus_2 (
  input  S2,
  input  S1,
  input  S0,
  input  Clk,
  input  INR,
  input  LD,
  input  CLR
);

  wire ac_control_1_clr, ac_control_1_inr, ac_control_1_ld, ar_control_1_clr, ar_control_1_inr,
       ar_control_1_ld, dr_control_1_clr, dr_control_1_inr, dr_control_1_ld, ir_control_1_ld,
       memory_control_1_read, memory_control_1_write, outr_control_1_ld, pc_control_1_clr, pc_control_1_inr,
       pc_control_1_ld, tr_control_1_clr, tr_control_1_inr, tr_control_1_ld;
  wire [5:0] multiplexer_1_out;
  wire [9:0] AR_p3, PC_p6;
  wire [11:0] AR_p6;
  wire [15:0] AC_d, DR_d, IR_q, Memory_d, TR_d;

  pc_control pc_control_1 (.ld(pc_control_1_ld), .clr(pc_control_1_clr), .INR(pc_control_1_inr));
  dr_control dr_control_1 (.ld(dr_control_1_ld), .clr(dr_control_1_clr), .INR(dr_control_1_inr));
  outr_control outr_control_1 (.ld(outr_control_1_ld));
  ar_control ar_control_1 (.ld(ar_control_1_ld), .clr(ar_control_1_clr), .INR(ar_control_1_inr));
  alu alu_1 ();
  tr_control tr_control_1 (.ld(tr_control_1_ld), .clr(tr_control_1_clr), .INR(tr_control_1_inr));
  ac_control ac_control_1 (.ld(ac_control_1_ld), .clr(ac_control_1_clr), .INR(ac_control_1_inr));
  ir_control ir_control_1 (.ld(ir_control_1_ld));
  memory_control memory_control_1 (.Write(memory_control_1_write), .Read(memory_control_1_read));
  Register OUTR (.D(AR_p3[0]), .C(Clk), .en(outr_control_1_ld));  // open: Q
  RAMDualPort #(.AddrBits(12), .Bits(16)) Memory (
    .A(AR_p6), .Din({multiplexer_1_out, AR_p3}), .str(memory_control_1_write), .C(Clk),
    .ld(memory_control_1_read), .D(Memory_d));
  // address_register_with_increment AR: pin names not known; wires that end beside it: ar_control_1_inr, Clk, AR_p3, ar_control_1_ld, ar_control_1_clr, AR_p6
  // address_register_with_increment PC: pin names not known; wires that end beside it: pc_control_1_inr, Clk, AR_p3, pc_control_1_ld, pc_control_1_clr, PC_p6
  _16_bit_register DR (
    .INR(dr_control_1_inr), .CLK(Clk), .Din({multiplexer_1_out, AR_p3}), .ld(dr_control_1_ld),
    .clr(dr_control_1_clr), .D(DR_d));
  _16_bit_register AC (
    .INR(ac_control_1_inr), .ld(ac_control_1_ld), .clr(ac_control_1_clr), .D(AC_d));  // open: CLK, Din
  Register #(.Bits(16)) IR (.D({multiplexer_1_out, AR_p3}), .C(Clk), .en(ir_control_1_ld), .Q(IR_q));
  _16_bit_register TR (
    .INR(tr_control_1_inr), .CLK(Clk), .Din({multiplexer_1_out, AR_p3}), .ld(tr_control_1_ld),
    .clr(tr_control_1_clr), .D(TR_d));
  Multiplexer #(.Selector_Bits(3), .Bits(16)) multiplexer_1 (
    .sel({S2, S1, S0}), .in_1({multiplexer_1_out, AR_p6[9:0]}), .in_2({multiplexer_1_out, PC_p6}),
    .in_3(DR_d), .in_4(AC_d), .in_5(IR_q), .in_6(TR_d), .in_7(Memory_d), .out({multiplexer_1_out, AR_p3}));  // open: in_0
  // Pins of 1 and 16 bits meet at {multiplexer_1_out, AR_p3}
  // Pins of 10 and 12 bits meet at AR_p6
endmodule
