// Digital circuit instruction_decoder.dig as structural Verilog
module instruction_decoder (
  input  IR_0,
  input  IR_1,
  input  IR_2,
  input  IR_3,
  input  IR_4,
  input  IR_5,
  input  IR_6,
  input  IR_7,
  input  IR_8,
  input  IR_9,
  input  IR_10,
  input  IR_11,
  input  IR_12,
  input  IR_13,
  input  IR_14,
  input  IR_15
);

  wire D0, D1, D2, D3, D4, D5, D6, D7, D8, D9, D10, D11, D12, D13, D14, D15, I0, I1, P0, P1, P2, P3, P4, P5,
       P6, P7, P8, P9, P10, P11, P12, P13, P14, P15, q, r, T3;

  Decoder #(.Selector_Bits(4)) decoder_1 (
    .sel({IR_13, IR_12, IR_11, IR_10}), .out_0(D0), .out_1(D1), .out_2(D2), .out_3(D3), .out_4(D4),
    .out_5(D5), .out_6(D6), .out_7(D7), .out_8(D8), .out_9(D9), .out_10(D10), .out_11(D11), .out_12(D12),
    .out_13(D13), .out_14(D14), .out_15(D15));
  Decoder #(.Selector_Bits(4)) decoder_2 (
    .sel({IR_3, IR_2, IR_1, IR_0}), .out_0(P0), .out_1(P1), .out_2(P2), .out_3(P3), .out_4(P4), .out_5(P5),
    .out_6(P6), .out_7(P7), .out_8(P8), .out_9(P9), .out_10(P10), .out_11(P11), .out_12(P12), .out_13(P13),
    .out_14(P14), .out_15(P15));
  and and_1 (r, D0, I0, I1, T3);
  and and_2 (q, D15, I0, I1, T3);
endmodule
