// Digital circuit memory_control.dig as structural Verilog
module memory_control (
  output Write,
  output Read
);

  wire and_1_out, and_2_out, and_3_out, and_4_out, and_5_out, D5, D7, D8, I0, or_1_out, R, R_t, T1, T4, T5,
       T6;

  or or_1 (or_1_out, D5, D7);
  and and_1 (and_1_out, R, T1);
  and and_2 (and_2_out, T5, or_1_out);
  and and_3 (and_3_out, D8, T6);
  and and_4 (and_4_out, R_t, T1);
  and and_5 (and_5_out, I0, T4);
  or or_2 (Write, and_1_out, and_2_out, and_3_out);
  or or_3 (Read, and_4_out, and_5_out);
endmodule
