// Digital circuit selection_logic_for_AC.dig as structural Verilog
module selection_logic_for_AC (
  output out_1
);

  wire and_1_out, and_2_out, D5, P1, q, T5;

  and and_1 (and_1_out, q, P1);
  and and_2 (and_2_out, D5, T5);
  or or_1 (out_1, and_1_out, and_2_out);
endmodule
