// Digital circuit selection_logic_for_PC.dig as structural Verilog
module selection_logic_for_PC (
  output out_1
);

  wire and_1_out, and_2_out, and_3_out, and_4_out, D5, R, R_t, T0, T1, T2, T4;

  and and_1 (and_1_out, R_t, T0);
  and and_2 (and_2_out, R_t, T1);
  and and_3 (and_3_out, D5, T4);
  and and_4 (and_4_out, R, T2);
  or or_1 (out_1, and_1_out, and_2_out, and_3_out, and_4_out);
endmodule
